// Digital circuit RippleCarryAdder.dig as structural Verilog
module RippleCarryAdder (
  input  A0,
  input  A1,
  input  A2,
  input  A3,
  input  B0,
  input  B1,
  input  B2,
  input  B3,
  input  C_in,
  output S0,
  output S1,
  output S2,
  output S3,
  output C_Out
);

  Add Adder3 (.a(A1), .c_i(A3));  // open: b, s, c_o
  Add Adder2 (.a(B2), .c_i(A2));  // open: b, s, c_o
  Add Adder1 (.a(B1), .c_i(A1));  // open: b, s, c_o
  Add Adder0 (.a(B0), .c_i(A0));  // open: b, s, c_o

  assign B3 = A1;
endmodule

/* Test case:
A3	A2	A1	A0	B3	B2	B1	B0	C_Out	S3	S2	S1	S0
0	0	0	0	0	0	0	0	0	0	0	0	0
0	0	0	1	0	0	0	0	0	0	0	0	1
0	0	1	0	0	0	0	0	0	0	0	1	0
0	0	1	1	0	0	0	0	0	0	0	1	1
0	1	0	0	0	0	0	0	0	0	1	0	0
0	1	0	1	0	0	0	0	0	0	1	0	1
0	1	1	0	0	0	0	0	0	0	1	1	0
0	1	1	1	0	0	0	0	0	0	1	1	1
1	0	0	0	0	0	0	0	0	1	0	0	0
1	0	0	1	0	0	0	0	0	1	0	0	1
1	0	1	0	0	0	0	0	0	1	0	1	0
1	0	1	1	0	0	0	0	0	1	0	1	1
1	1	0	0	0	0	0	0	0	1	1	0	0
1	1	0	1	0	0	0	0	0	1	1	0	1
1	1	1	0	0	0	0	0	0	1	1	1	0
1	1	1	1	0	0	0	0	0	1	1	1	1
0	0	0	0	0	0	0	1	0	0	0	0	1
0	0	0	1	0	0	0	1	0	0	0	1	0
0	0	1	0	0	0	0	1	0	0	0	1	1
0	0	1	1	0	0	0	1	0	0	1	0	0
0	1	0	0	0	0	0	1	0	0	1	0	1
0	1	0	1	0	0	0	1	0	0	1	1	0
0	1	1	0	0	0	0	1	0	0	1	1	1
0	1	1	1	0	0	0	1	0	1	0	0	0
1	0	0	0	0	0	0	1	0	1	0	0	1
1	0	0	1	0	0	0	1	0	1	0	1	0
1	0	1	0	0	0	0	1	0	1	0	1	1
1	0	1	1	0	0	0	1	0	1	1	0	0
1	1	0	0	0	0	0	1	0	1	1	0	1
1	1	0	1	0	0	0	1	0	1	1	1	0
1	1	1	0	0	0	0	1	0	1	1	1	1
1	1	1	1	0	0	0	1	1	0	0	0	0
0	0	0	0	0	0	1	0	0	0	0	1	0
0	0	0	1	0	0	1	0	0	0	0	1	1
0	0	1	0	0	0	1	0	0	0	1	0	0
0	0	1	1	0	0	1	0	0	0	1	0	1
0	1	0	0	0	0	1	0	0	0	1	1	0
0	1	0	1	0	0	1	0	0	0	1	1	1
0	1	1	0	0	0	1	0	0	1	0	0	0
0	1	1	1	0	0	1	0	0	1	0	0	1
1	0	0	0	0	0	1	0	0	1	0	1	0
1	0	0	1	0	0	1	0	0	1	0	1	1
1	0	1	0	0	0	1	0	0	1	1	0	0
1	0	1	1	0	0	1	0	0	1	1	0	1
1	1	0	0	0	0	1	0	0	1	1	1	0
1	1	0	1	0	0	1	0	0	1	1	1	1
1	1	1	0	0	0	1	0	1	0	0	0	0
1	1	1	1	0	0	1	0	1	0	0	0	1
0	0	0	0	0	0	1	1	0	0	0	1	1
0	0	0	1	0	0	1	1	0	0	1	0	0
0	0	1	0	0	0	1	1	0	0	1	0	1
0	0	1	1	0	0	1	1	0	0	1	1	0
0	1	0	0	0	0	1	1	0	0	1	1	1
0	1	0	1	0	0	1	1	0	1	0	0	0
0	1	1	0	0	0	1	1	0	1	0	0	1
0	1	1	1	0	0	1	1	0	1	0	1	0
1	0	0	0	0	0	1	1	0	1	0	1	1
1	0	0	1	0	0	1	1	0	1	1	0	0
1	0	1	0	0	0	1	1	0	1	1	0	1
1	0	1	1	0	0	1	1	0	1	1	1	0
1	1	0	0	0	0	1	1	0	1	1	1	1
1	1	0	1	0	0	1	1	1	0	0	0	0
1	1	1	0	0	0	1	1	1	0	0	0	1
1	1	1	1	0	0	1	1	1	0	0	1	0
0	0	0	0	0	1	0	0	0	0	1	0	0
0	0	0	1	0	1	0	0	0	0	1	0	1
0	0	1	0	0	1	0	0	0	0	1	1	0
0	0	1	1	0	1	0	0	0	0	1	1	1
0	1	0	0	0	1	0	0	0	1	0	0	0
0	1	0	1	0	1	0	0	0	1	0	0	1
0	1	1	0	0	1	0	0	0	1	0	1	0
0	1	1	1	0	1	0	0	0	1	0	1	1
1	0	0	0	0	1	0	0	0	1	1	0	0
1	0	0	1	0	1	0	0	0	1	1	0	1
1	0	1	0	0	1	0	0	0	1	1	1	0
1	0	1	1	0	1	0	0	0	1	1	1	1
1	1	0	0	0	1	0	0	1	0	0	0	0
1	1	0	1	0	1	0	0	1	0	0	0	1
1	1	1	0	0	1	0	0	1	0	0	1	0
1	1	1	1	0	1	0	0	1	0	0	1	1
0	0	0	0	0	1	0	1	0	0	1	0	1
0	0	0	1	0	1	0	1	0	0	1	1	0
0	0	1	0	0	1	0	1	0	0	1	1	1
0	0	1	1	0	1	0	1	0	1	0	0	0
0	1	0	0	0	1	0	1	0	1	0	0	1
0	1	0	1	0	1	0	1	0	1	0	1	0
0	1	1	0	0	1	0	1	0	1	0	1	1
0	1	1	1	0	1	0	1	0	1	1	0	0
1	0	0	0	0	1	0	1	0	1	1	0	1
1	0	0	1	0	1	0	1	0	1	1	1	0
1	0	1	0	0	1	0	1	0	1	1	1	1
1	0	1	1	0	1	0	1	1	0	0	0	0
1	1	0	0	0	1	0	1	1	0	0	0	1
1	1	0	1	0	1	0	1	1	0	0	1	0
1	1	1	0	0	1	0	1	1	0	0	1	1
1	1	1	1	0	1	0	1	1	0	1	0	0
0	0	0	0	0	1	1	0	0	0	1	1	0
0	0	0	1	0	1	1	0	0	0	1	1	1
0	0	1	0	0	1	1	0	0	1	0	0	0
0	0	1	1	0	1	1	0	0	1	0	0	1
0	1	0	0	0	1	1	0	0	1	0	1	0
0	1	0	1	0	1	1	0	0	1	0	1	1
0	1	1	0	0	1	1	0	0	1	1	0	0
0	1	1	1	0	1	1	0	0	1	1	0	1
1	0	0	0	0	1	1	0	0	1	1	1	0
1	0	0	1	0	1	1	0	0	1	1	1	1
1	0	1	0	0	1	1	0	1	0	0	0	0
1	0	1	1	0	1	1	0	1	0	0	0	1
1	1	0	0	0	1	1	0	1	0	0	1	0
1	1	0	1	0	1	1	0	1	0	0	1	1
1	1	1	0	0	1	1	0	1	0	1	0	0
1	1	1	1	0	1	1	0	1	0	1	0	1
0	0	0	0	0	1	1	1	0	0	1	1	1
0	0	0	1	0	1	1	1	0	1	0	0	0
0	0	1	0	0	1	1	1	0	1	0	0	1
0	0	1	1	0	1	1	1	0	1	0	1	0
0	1	0	0	0	1	1	1	0	1	0	1	1
0	1	0	1	0	1	1	1	0	1	1	0	0
0	1	1	0	0	1	1	1	0	1	1	0	1
0	1	1	1	0	1	1	1	0	1	1	1	0
1	0	0	0	0	1	1	1	0	1	1	1	1
1	0	0	1	0	1	1	1	1	0	0	0	0
1	0	1	0	0	1	1	1	1	0	0	0	1
1	0	1	1	0	1	1	1	1	0	0	1	0
1	1	0	0	0	1	1	1	1	0	0	1	1
1	1	0	1	0	1	1	1	1	0	1	0	0
1	1	1	0	0	1	1	1	1	0	1	0	1
1	1	1	1	0	1	1	1	1	0	1	1	0
0	0	0	0	1	0	0	0	0	1	0	0	0
0	0	0	1	1	0	0	0	0	1	0	0	1
0	0	1	0	1	0	0	0	0	1	0	1	0
0	0	1	1	1	0	0	0	0	1	0	1	1
0	1	0	0	1	0	0	0	0	1	1	0	0
0	1	0	1	1	0	0	0	0	1	1	0	1
0	1	1	0	1	0	0	0	0	1	1	1	0
0	1	1	1	1	0	0	0	0	1	1	1	1
1	0	0	0	1	0	0	0	1	0	0	0	0
1	0	0	1	1	0	0	0	1	0	0	0	1
1	0	1	0	1	0	0	0	1	0	0	1	0
1	0	1	1	1	0	0	0	1	0	0	1	1
1	1	0	0	1	0	0	0	1	0	1	0	0
1	1	0	1	1	0	0	0	1	0	1	0	1
1	1	1	0	1	0	0	0	1	0	1	1	0
1	1	1	1	1	0	0	0	1	0	1	1	1
0	0	0	0	1	0	0	1	0	1	0	0	1
0	0	0	1	1	0	0	1	0	1	0	1	0
0	0	1	0	1	0	0	1	0	1	0	1	1
0	0	1	1	1	0	0	1	0	1	1	0	0
0	1	0	0	1	0	0	1	0	1	1	0	1
0	1	0	1	1	0	0	1	0	1	1	1	0
0	1	1	0	1	0	0	1	0	1	1	1	1
0	1	1	1	1	0	0	1	1	0	0	0	0
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*/
